# Fritzing sketch schematic (saved by Fritzing 0.9.3b)
breadboards: 1

parts:
  Raspberry_Pi_Zero1 = Raspberry Pi Zero
  DS1 = DS18B20 1-Wire Temperature Sensor [part_number=DS18B20]
  R1 = Resistor [tolerance=±5% resistance=4.7k package="0805 [SMD]"]

nets:
  3V3: Raspberry_Pi_Zero1.3v3, Raspberry_Pi_Zero1.3V3, DS1.VDD, R1.Pin_0
  N1: Raspberry_Pi_Zero1.GIPO4, DS1.DQ, R1.Pin_1
  GND: Raspberry_Pi_Zero1.GND, DS1.GND
